# Fritzing sketch lightmeter001 (saved by Fritzing 0.9.0b)
circuit board: 9.89511cm x 5.82529cm
breadboards: 1

parts:
  Part1 = Arduino Nano (Rev3.0)
  Part2 = BH1750
  Nokia_5110_LCD_Module1 = Nokia5110LCDModule
  R1 = Resistor [tolerance=±5% resistance=330 package=THT]
  R2 = Resistor [tolerance=±5% resistance=4.7k package=THT]
  S1 = Pushbutton [package="[THT]"]
  S2 = Pushbutton [package="[THT]"]
  R3 = Resistor [tolerance=±5% resistance=4.7k package=THT]
  R4 = Resistor [tolerance=±5% resistance=4.7k package=THT]
  S3 = Pushbutton [package="[THT]"]

nets:
  GND: Part1.GND, Part2.GND, Part2.ADDR, Nokia_5110_LCD_Module1.RST, S1.Pin_3, S1.Pin_4, S2.Pin_3, S2.Pin_4, S3.Pin_3, S3.Pin_4
  N1: Part1.D2, R4.Pin_0, S3.Pin_1, S3.Pin_2
  N2: Part1.D3, S2.Pin_1, S2.Pin_2, R3.Pin_0
  N3: Part1.D4, R2.Pin_0, S1.Pin_1, S1.Pin_2
  N4: Part1.D5, Nokia_5110_LCD_Module1.DIN
  N5: Part1.D6, Nokia_5110_LCD_Module1.D/C
  N6: Part1.D7, Nokia_5110_LCD_Module1.CS
  N7: Part1.D9, R1.Pin_1
  N8: Part1.D11/MOSI, Nokia_5110_LCD_Module1.CLK
  5V: Part1.5V, Part2.VCC, Nokia_5110_LCD_Module1.LED, R2.Pin_1, R3.Pin_1, R4.Pin_1
  N9: Part1.A5, Part2.SCL
  N10: Part1.A4, Part2.SDA
  N11: Part1.D13/SCK, Nokia_5110_LCD_Module1.Vcc
  N12: Nokia_5110_LCD_Module1.Gnd, R1.Pin_0

notes:
  Buttons: MODE, ISO, VALUE
  Nokia 5510 LCD
  Arduino Nano

custom parts:
  BH1750: Light Sensor
  : Nokia 5110 LCD with 8 pin. It's a 1.94in*1.66in module part. Description: The Nokia 5110 is a basic graphic LCD screen for lots of applications. It was originally intended for as a cell phone screen. This one is mounted on an easy to solder PCB. It uses the PCD8544 controller. The PCD8544 is a low power CMOS LCD controller/driver, designed to drive a graphic display of 48 rows and 84 columns.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
